# Fritzing sketch led-foot-hardware-setup (saved by Fritzing 0.9.6b)
breadboards: 1
perfboards: 3

parts:
  Part1 = Arduino Mega 2560 (Rev3)
  Q1 = Basic FET P-Channel [package="TO220 [THT]"]
  Q2 = Basic FET P-Channel [package="TO220 [THT]"]
  Q3 = Basic FET P-Channel [package="TO220 [THT]"]
  Q4 = Basic FET P-Channel [package="TO220 [THT]"]
  D1 = Diode [package=diode-hv]
  D2 = Diode [package=diode-hv]
  D3 = Diode [package=diode-hv]
  U1 = RELAY [package=relay-jzc]
  U2 = RELAY [package=relay-jzc]
  U3 = RELAY [package=relay-jzc]
  Power_plug1 = Power plug

nets:
  GND: Part1.GND, Q1.source, Q2.source, Q3.source, Q4.source, U1.NC, U2.NC, U3.NC, Power_plug1.GND
  N1: Part1.D12_PWM, Q4.gate
  N2: Part1.D11_PWM, Q3.gate
  N3: Part1.5V, D1.A, D2.A, D3.A
  N4: Part1.D5_PWM, Q1.gate
  N5: Part1.D6_PWM, Q2.gate
  N6: Part1.D24, U1.NO
  N7: Part1.D26, U2.NO
  N8: Part1.D28, U3.NO
  N9: U1.COIL1, U2.COIL1, U3.COIL1, Power_plug1.VCC

notes:
  room 1
  room 2
  room 3
  12V Power
